// Logisim project main0.circ as structural Verilog: 13 circuits, main circuit main0
module main0 (
  input  [7:0] in_1,
  input  [7:0] in_2,
  input  [7:0] in_3,
  input  [7:0] in_4,
  input  [7:0] in_5,
  input  [7:0] in_6,
  input  [7:0] in_7,
  input  [7:0] in_8,
  input  [7:0] in_9,
  input  reset
);

  wire a, and_1_out, and_2_out, and_3_out, and_4_out, and_5_out, and_6_out, and_7_out, and_8_out, and_9_out,
       and_10_out, and_11_out, and_12_out, and_13_out, and_14_out, and_15_out, and_16_out, and_17_out,
       and_18_out, and_19_out, and_20_out, and_21_out, and_22_out, clock_1_out, display_decoder_1_a,
       display_decoder_1_b, display_decoder_1_c, display_decoder_1_d, display_decoder_1_e,
       display_decoder_1_f, display_decoder_1_g, display_decoder_1_h, display_decoder_2_a,
       display_decoder_2_b, display_decoder_2_c, display_decoder_2_d, display_decoder_2_e,
       display_decoder_2_f, display_decoder_2_g, display_decoder_2_h, fulladder_8_bit_1_s0,
       fulladder_8_bit_1_s1, fulladder_8_bit_1_s2, fulladder_8_bit_1_s3, fulladder_8_bit_1_s4,
       fulladder_8_bit_1_s5, fulladder_8_bit_1_s6, fulladder_8_bit_1_s7, fulladder_8_bit_2_s4,
       fulladder_8_bit_2_s5, fulladder_8_bit_2_s6, fulladder_8_bit_2_s7, multiplexer_2_out, not_1_out,
       not_2_out, not_3_out, not_4_out, not_5_out, not_6_out, not_7_out, not_8_out, not_9_out, not_10_out,
       not_11_out, not_12_out, not_13_out, xnor_1_out, xnor_2_out, xnor_3_out, xnor_4_out, xnor_5_out,
       xnor_6_out, xnor_7_out, xnor_8_out;
  wire [1:0] multiplexer_5_out;
  wire [3:0] counter_1_q, fulladder_8_bit_2_s0, multiplexer_3_out, ram4x4_1_s0, register_1_q;
  wire [7:0] multiplexer_1_out, multiplexer_4_out, register_8_bit_1_q0, register_8_bit_2_q0,
       register_8_bit_3_q0, register_8_bit_4_q0;

  Clock clock_1 (.out(clock_1_out));
  not not_1 (not_1_out, multiplexer_2_out);
  and and_1 (and_1_out, and_4_out, not_1_out);
  Counter #(.max('hf), .width(4)) counter_1 (
    .load(and_1_out), .D(multiplexer_1_out[5:2]), .Q(counter_1_q), .up(1'b1), .clk(clock_1_out), .clr(reset));  // open: count, carry
  Multiplexer #(.select(4), .width(8)) multiplexer_1 (
    .in0(in_1), .in1(in_2), .in2(in_3), .in3(in_4), .in4(in_5), .in5(in_6), .in6(in_7), .in7(in_8),
    .in8(in_9), .out(multiplexer_1_out), .sel(register_1_q));  // open: in9, in10, in11, in12, in13, in14, in15
  Register #(.trigger("falling"), .width(4)) register_1 (
    .D(counter_1_q), .en(1'b1), .clk(clock_1_out), .Q(register_1_q), .clr(reset));
  not not_2 (not_2_out, multiplexer_1_out[6]);
  not not_3 (not_3_out, multiplexer_1_out[7]);
  and and_2 (and_2_out, multiplexer_1_out[6], not_3_out);
  and and_3 (and_3_out, multiplexer_1_out[7], not_2_out);
  display_decoder display_decoder_1 (
    .A0(multiplexer_4_out[0]), .A1(multiplexer_4_out[1]), .A2(multiplexer_4_out[2]),
    .A3(multiplexer_4_out[3]), .a(display_decoder_1_a), .b(display_decoder_1_b), .c(display_decoder_1_c),
    .d(display_decoder_1_d), .e(display_decoder_1_e), .f(display_decoder_1_f), .g(display_decoder_1_g),
    .h(display_decoder_1_h));
  display_decoder display_decoder_2 (
    .A0(multiplexer_4_out[4]), .A1(multiplexer_4_out[5]), .A2(multiplexer_4_out[6]),
    .A3(multiplexer_4_out[7]), .a(display_decoder_2_a), .b(display_decoder_2_b), .c(display_decoder_2_c),
    .d(display_decoder_2_d), .e(display_decoder_2_e), .f(display_decoder_2_f), .g(display_decoder_2_g),
    .h(display_decoder_2_h));
  not not_4 (not_4_out, multiplexer_1_out[4]);
  not not_5 (not_5_out, multiplexer_1_out[5]);
  not not_6 (not_6_out, multiplexer_1_out[4]);
  not not_7 (not_7_out, multiplexer_1_out[5]);
  not not_8 (not_8_out, multiplexer_1_out[6]);
  and and_4 (and_4_out, multiplexer_1_out[7], multiplexer_1_out[6]);
  and and_5 (and_5_out, not_4_out, not_5_out);
  and and_6 (and_6_out, multiplexer_1_out[5], not_6_out);
  and and_7 (and_7_out, not_7_out, multiplexer_1_out[4]);
  and and_8 (and_8_out, multiplexer_1_out[5], multiplexer_1_out[4]);
  and and_9 (and_9_out, and_3_out, clock_1_out);
  not not_9 (not_9_out, multiplexer_1_out[7]);
  not not_10 (not_10_out, multiplexer_1_out[6]);
  and and_10 (and_10_out, multiplexer_1_out[7], multiplexer_1_out[6]);
  not not_11 (not_11_out, and_10_out);
  and and_11 (and_11_out, multiplexer_1_out[7], not_8_out);
  and and_12 (and_12_out, not_9_out, not_10_out);
  Multiplexer #(.select(4)) multiplexer_2 (
    .in0(1'b0), .in1(1'b0), .in2(1'b0), .in3(1'b0), .in4(1'b0), .in5(1'b0), .in6(and_14_out),
    .in7(and_22_out), .in8(1'b0), .in9(1'b0), .in10(1'b0), .in11(1'b0), .in12(1'b0), .in13(1'b0),
    .in14(1'b0), .in15(1'b0), .out(multiplexer_2_out), .sel(register_1_q));
  _7_Segment_Display u_7_segment_display_1 (
    .g(display_decoder_2_g), .f(display_decoder_2_f), .a(display_decoder_2_a), .b(display_decoder_2_b),
    .e(display_decoder_2_e), .d(display_decoder_2_d), .c(display_decoder_2_c), .dp(display_decoder_2_h));
  and and_13 (and_13_out, and_6_out, and_12_out);
  RAM4x4 ram4x4_1 (
    .D1(multiplexer_1_out[1]), .D3(multiplexer_1_out[3]), .D2(multiplexer_1_out[2]),
    .D0(multiplexer_1_out[0]), .addr1(multiplexer_1_out[4]), .addr0(multiplexer_1_out[5]), .EN(and_9_out),
    .reset(reset), .S0(ram4x4_1_s0[0]), .S2(ram4x4_1_s0[1]), .S3(ram4x4_1_s0[2]), .S1(ram4x4_1_s0[3]));
  _7_Segment_Display u_7_segment_display_2 (
    .g(display_decoder_1_g), .f(display_decoder_1_f), .a(display_decoder_1_a), .b(display_decoder_1_b),
    .e(display_decoder_1_e), .d(display_decoder_1_d), .c(display_decoder_1_c), .dp(display_decoder_1_h));
  Multiplexer #(.width(4)) multiplexer_3 (
    .in0(fulladder_8_bit_2_s0), .in1(ram4x4_1_s0), .out(multiplexer_3_out), .sel(and_11_out));
  and and_14 (and_14_out, and_4_out, and_18_out);
  and and_15 (and_15_out, clock_1_out, not_11_out, and_7_out);
  Multiplexer #(.select(2), .width(8)) multiplexer_4 (
    .in0({register_8_bit_1_q0[7], a, register_8_bit_1_q0[5:0]}), .in1(register_8_bit_4_q0),
    .in2(register_8_bit_2_q0), .in3(register_8_bit_3_q0), .out(multiplexer_4_out), .sel(multiplexer_5_out));
  Multiplexer #(.width(2)) multiplexer_5 (
    .in1(multiplexer_1_out[5:4]), .out(multiplexer_5_out), .sel(and_2_out));  // open: in0
  and and_16 (and_16_out, and_13_out, clock_1_out);
  not not_12 (not_12_out, and_5_out);
  not not_13 (not_13_out, not_12_out);
  register_8_bit register_8_bit_1 (
    .reset(reset), .EN(not_13_out), .D0(ram4x4_1_s0[0]), .D1(ram4x4_1_s0[3]), .D2(ram4x4_1_s0[1]),
    .D3(ram4x4_1_s0[2]), .Q0(register_8_bit_1_q0[0]), .Q1(register_8_bit_1_q0[1]),
    .Q2(register_8_bit_1_q0[2]), .Q3(register_8_bit_1_q0[3]), .Q4(register_8_bit_1_q0[4]),
    .Q5(register_8_bit_1_q0[5]), .Q6(a), .Q7(register_8_bit_1_q0[7]));  // open: D4, D5, D6, D7
  register_8_bit register_8_bit_2 (
    .reset(reset), .EN(and_16_out), .D0(fulladder_8_bit_1_s0), .D1(fulladder_8_bit_1_s1),
    .D2(fulladder_8_bit_1_s2), .D3(fulladder_8_bit_1_s3), .D4(fulladder_8_bit_1_s4),
    .D5(fulladder_8_bit_1_s5), .D6(fulladder_8_bit_1_s6), .D7(fulladder_8_bit_1_s7),
    .Q0(register_8_bit_2_q0[0]), .Q1(register_8_bit_2_q0[1]), .Q2(register_8_bit_2_q0[2]),
    .Q3(register_8_bit_2_q0[3]), .Q4(register_8_bit_2_q0[4]), .Q5(register_8_bit_2_q0[5]),
    .Q6(register_8_bit_2_q0[6]), .Q7(register_8_bit_2_q0[7]));
  register_8_bit register_8_bit_3 (
    .reset(reset), .EN(and_8_out), .D0(ram4x4_1_s0[0]), .D1(ram4x4_1_s0[3]), .D2(ram4x4_1_s0[1]),
    .D3(ram4x4_1_s0[2]), .Q0(register_8_bit_3_q0[0]), .Q1(register_8_bit_3_q0[1]),
    .Q2(register_8_bit_3_q0[2]), .Q3(register_8_bit_3_q0[3]), .Q4(register_8_bit_3_q0[4]),
    .Q5(register_8_bit_3_q0[5]), .Q6(register_8_bit_3_q0[6]), .Q7(register_8_bit_3_q0[7]));  // open: D4, D5, D6, D7
  register_8_bit register_8_bit_4 (
    .reset(reset), .EN(and_15_out), .D0(multiplexer_3_out[0]), .D1(multiplexer_3_out[1]),
    .D2(multiplexer_3_out[2]), .D3(multiplexer_3_out[3]), .D4(fulladder_8_bit_2_s4),
    .D5(fulladder_8_bit_2_s5), .D6(fulladder_8_bit_2_s6), .D7(fulladder_8_bit_2_s7),
    .Q0(register_8_bit_4_q0[0]), .Q1(register_8_bit_4_q0[1]), .Q2(register_8_bit_4_q0[2]),
    .Q3(register_8_bit_4_q0[3]), .Q4(register_8_bit_4_q0[4]), .Q5(register_8_bit_4_q0[5]),
    .Q6(register_8_bit_4_q0[6]), .Q7(register_8_bit_4_q0[7]));
  xnor xnor_1 (xnor_1_out, register_8_bit_4_q0[3], register_8_bit_1_q0[3]);
  xnor xnor_2 (xnor_2_out, register_8_bit_4_q0[2], register_8_bit_1_q0[2]);
  and and_17 (and_17_out, xnor_1_out, xnor_2_out);
  xnor xnor_3 (xnor_3_out, register_8_bit_4_q0[1], register_8_bit_1_q0[1]);
  and and_18 (and_18_out, and_17_out, and_19_out);
  xnor xnor_4 (xnor_4_out, register_8_bit_4_q0[0], register_8_bit_1_q0[0]);
  and and_19 (and_19_out, xnor_3_out, xnor_4_out);
  fulladder_8_bit fulladder_8_bit_1 (
    .A0(register_8_bit_4_q0[0]), .A1(register_8_bit_4_q0[1]), .A2(register_8_bit_4_q0[2]),
    .A3(register_8_bit_4_q0[3]), .A4(register_8_bit_4_q0[4]), .A5(register_8_bit_4_q0[5]),
    .A6(register_8_bit_4_q0[6]), .A7(register_8_bit_4_q0[7]), .B0(register_8_bit_2_q0[0]),
    .B1(register_8_bit_2_q0[1]), .B2(register_8_bit_2_q0[2]), .B3(register_8_bit_2_q0[3]),
    .B4(register_8_bit_2_q0[4]), .B5(register_8_bit_2_q0[5]), .B6(register_8_bit_2_q0[6]),
    .B7(register_8_bit_2_q0[7]), .S0(fulladder_8_bit_1_s0), .S1(fulladder_8_bit_1_s1),
    .S2(fulladder_8_bit_1_s2), .S3(fulladder_8_bit_1_s3), .S4(fulladder_8_bit_1_s4),
    .S5(fulladder_8_bit_1_s5), .S6(fulladder_8_bit_1_s6), .S7(fulladder_8_bit_1_s7));  // open: Light
  fulladder_8_bit fulladder_8_bit_2 (
    .A0(register_8_bit_3_q0[0]), .A1(register_8_bit_3_q0[1]), .A2(register_8_bit_3_q0[2]),
    .A3(register_8_bit_3_q0[3]), .A4(register_8_bit_3_q0[4]), .A5(register_8_bit_3_q0[5]),
    .A6(register_8_bit_3_q0[6]), .A7(register_8_bit_3_q0[7]), .B0(register_8_bit_4_q0[0]),
    .B1(register_8_bit_4_q0[1]), .B2(register_8_bit_4_q0[2]), .B3(register_8_bit_4_q0[3]),
    .B4(register_8_bit_4_q0[4]), .B5(register_8_bit_4_q0[5]), .B6(register_8_bit_4_q0[6]),
    .B7(register_8_bit_4_q0[7]), .S0(fulladder_8_bit_2_s0[0]), .S1(fulladder_8_bit_2_s0[1]),
    .S2(fulladder_8_bit_2_s0[2]), .S3(fulladder_8_bit_2_s0[3]), .S4(fulladder_8_bit_2_s4),
    .S5(fulladder_8_bit_2_s5), .S6(fulladder_8_bit_2_s6), .S7(fulladder_8_bit_2_s7));  // open: Light
  xnor xnor_5 (xnor_5_out, register_8_bit_1_q0[3], register_8_bit_3_q0[0]);
  xnor xnor_6 (xnor_6_out, register_8_bit_1_q0[2], register_8_bit_3_q0[1]);
  and and_20 (and_20_out, xnor_5_out, xnor_6_out);
  xnor xnor_7 (xnor_7_out, register_8_bit_1_q0[1], register_8_bit_3_q0[2]);
  and and_21 (and_21_out, xnor_7_out, xnor_8_out);
  and and_22 (and_22_out, and_20_out, and_21_out);
  xnor xnor_8 (xnor_8_out, register_8_bit_1_q0[0], register_8_bit_3_q0[3]);

  // Notes on the sheet:
  //   out:  |01|[rs]|0000
  //   0:   li: r0,11                                    10001011
  //   1:   li: r1,1                                      10010001
  //   2:   li: r2,0                                      10100000
  //   3:   li : r3,2                                     10110010
  //   4:   add r2,r2,r1                            00101001  
  //   5:   add r1,r1,r3                            00010111
  //   6:   bner0 r1,4                              11010001
  //   7：out rs2                                    01100000
  //   8:   bner0 r3,7                           11011111
endmodule

module RAM4x4 (
  input  D1,
  input  D3,
  input  D2,
  input  D0,
  input  addr1,
  input  addr0,
  input  EN,
  input  reset,
  output S0,
  output S2,
  output S3,
  output S1
);

  wire and_1_out, and_2_out, and_3_out, and_4_out, and_5_out, and_6_out, and_7_out, and_8_out, and_9_out,
       and_10_out, and_11_out, and_12_out, and_13_out, and_14_out, and_15_out, and_16_out, and_17_out,
       and_18_out, and_19_out, and_20_out, decoder_2_4_1_out_3, decoder_2_4_1_out_4, decoder_2_4_1_out_5,
       decoder_2_4_1_out_6, edge_triggereddflip_flop_1_q, edge_triggereddflip_flop_2_q,
       edge_triggereddflip_flop_3_q, edge_triggereddflip_flop_4_q, edge_triggereddflip_flop_5_q,
       edge_triggereddflip_flop_6_q, edge_triggereddflip_flop_7_q, edge_triggereddflip_flop_8_q,
       edge_triggereddflip_flop_9_q, edge_triggereddflip_flop_10_q, edge_triggereddflip_flop_11_q,
       edge_triggereddflip_flop_12_q, edge_triggereddflip_flop_13_q, edge_triggereddflip_flop_14_q,
       edge_triggereddflip_flop_15_q, edge_triggereddflip_flop_16_q;

  decoder_2_4 decoder_2_4_1 (
    .in_1(addr1), .in_2(addr0), .out_3(decoder_2_4_1_out_3), .out_4(decoder_2_4_1_out_4),
    .out_5(decoder_2_4_1_out_5), .out_6(decoder_2_4_1_out_6));
  and and_1 (and_1_out, decoder_2_4_1_out_3, EN);
  and and_2 (and_2_out, decoder_2_4_1_out_4, EN);
  and and_3 (and_3_out, decoder_2_4_1_out_5, EN);
  and and_4 (and_4_out, decoder_2_4_1_out_6, EN);
  Edge_TriggeredDFlip_Flop edge_triggereddflip_flop_1 (
    .D(D3), .CP(and_4_out), .reset(reset), .Q(edge_triggereddflip_flop_1_q));
  and and_5 (and_5_out, decoder_2_4_1_out_3, edge_triggereddflip_flop_2_q);
  Edge_TriggeredDFlip_Flop edge_triggereddflip_flop_2 (
    .D(D3), .CP(and_1_out), .reset(reset), .Q(edge_triggereddflip_flop_2_q));
  and and_6 (and_6_out, decoder_2_4_1_out_4, edge_triggereddflip_flop_3_q);
  Edge_TriggeredDFlip_Flop edge_triggereddflip_flop_3 (
    .D(D3), .CP(and_2_out), .reset(reset), .Q(edge_triggereddflip_flop_3_q));
  and and_7 (and_7_out, decoder_2_4_1_out_5, edge_triggereddflip_flop_4_q);
  Edge_TriggeredDFlip_Flop edge_triggereddflip_flop_4 (
    .D(D3), .CP(and_3_out), .reset(reset), .Q(edge_triggereddflip_flop_4_q));
  and and_8 (and_8_out, decoder_2_4_1_out_6, edge_triggereddflip_flop_1_q);
  or or_1 (S3, and_8_out, and_7_out, and_6_out, and_5_out);
  Edge_TriggeredDFlip_Flop edge_triggereddflip_flop_5 (
    .D(D2), .CP(and_1_out), .reset(reset), .Q(edge_triggereddflip_flop_5_q));
  and and_9 (and_9_out, decoder_2_4_1_out_4, edge_triggereddflip_flop_6_q);
  Edge_TriggeredDFlip_Flop edge_triggereddflip_flop_6 (
    .D(D2), .CP(and_2_out), .reset(reset), .Q(edge_triggereddflip_flop_6_q));
  and and_10 (and_10_out, decoder_2_4_1_out_5, edge_triggereddflip_flop_7_q);
  Edge_TriggeredDFlip_Flop edge_triggereddflip_flop_7 (
    .D(D2), .CP(and_3_out), .reset(reset), .Q(edge_triggereddflip_flop_7_q));
  and and_11 (and_11_out, decoder_2_4_1_out_6, edge_triggereddflip_flop_8_q);
  Edge_TriggeredDFlip_Flop edge_triggereddflip_flop_8 (
    .D(D2), .CP(and_4_out), .reset(reset), .Q(edge_triggereddflip_flop_8_q));
  and and_12 (and_12_out, decoder_2_4_1_out_3, edge_triggereddflip_flop_5_q);
  or or_2 (S2, and_11_out, and_10_out, and_9_out, and_12_out);
  Edge_TriggeredDFlip_Flop edge_triggereddflip_flop_9 (
    .D(D1), .CP(and_1_out), .reset(reset), .Q(edge_triggereddflip_flop_9_q));
  Edge_TriggeredDFlip_Flop edge_triggereddflip_flop_10 (
    .D(D1), .CP(and_2_out), .reset(reset), .Q(edge_triggereddflip_flop_10_q));
  Edge_TriggeredDFlip_Flop edge_triggereddflip_flop_11 (
    .D(D1), .CP(and_3_out), .reset(reset), .Q(edge_triggereddflip_flop_11_q));
  Edge_TriggeredDFlip_Flop edge_triggereddflip_flop_12 (
    .D(D1), .CP(and_4_out), .reset(reset), .Q(edge_triggereddflip_flop_12_q));
  and and_13 (and_13_out, decoder_2_4_1_out_3, edge_triggereddflip_flop_9_q);
  and and_14 (and_14_out, decoder_2_4_1_out_4, edge_triggereddflip_flop_10_q);
  and and_15 (and_15_out, decoder_2_4_1_out_5, edge_triggereddflip_flop_11_q);
  and and_16 (and_16_out, decoder_2_4_1_out_6, edge_triggereddflip_flop_12_q);
  or or_3 (S1, and_16_out, and_15_out, and_14_out, and_13_out);
  Edge_TriggeredDFlip_Flop edge_triggereddflip_flop_13 (
    .D(D0), .CP(and_1_out), .reset(reset), .Q(edge_triggereddflip_flop_13_q));
  and and_17 (and_17_out, decoder_2_4_1_out_4, edge_triggereddflip_flop_14_q);
  Edge_TriggeredDFlip_Flop edge_triggereddflip_flop_14 (
    .D(D0), .CP(and_2_out), .reset(reset), .Q(edge_triggereddflip_flop_14_q));
  and and_18 (and_18_out, decoder_2_4_1_out_5, edge_triggereddflip_flop_15_q);
  Edge_TriggeredDFlip_Flop edge_triggereddflip_flop_15 (
    .D(D0), .CP(and_3_out), .reset(reset), .Q(edge_triggereddflip_flop_15_q));
  Edge_TriggeredDFlip_Flop edge_triggereddflip_flop_16 (
    .D(D0), .CP(and_4_out), .reset(reset), .Q(edge_triggereddflip_flop_16_q));
  and and_19 (and_19_out, decoder_2_4_1_out_3, edge_triggereddflip_flop_13_q);
  and and_20 (and_20_out, decoder_2_4_1_out_6, edge_triggereddflip_flop_16_q);
  or or_4 (S0, and_20_out, and_18_out, and_17_out, and_19_out);
endmodule

module display_decoder (
  input  A0,
  input  A1,
  input  A2,
  input  A3,
  output a,
  output b,
  output c,
  output d,
  output e,
  output f,
  output g,
  output h
);

  wire decoder4_16_1_y0, decoder4_16_1_y1, decoder4_16_1_y2, decoder4_16_1_y3, decoder4_16_1_y4,
       decoder4_16_1_y5, decoder4_16_1_y6, decoder4_16_1_y7, decoder4_16_1_y8, decoder4_16_1_y9,
       decoder4_16_1_y10, decoder4_16_1_y11, decoder4_16_1_y12, decoder4_16_1_y13, decoder4_16_1_y14,
       decoder4_16_1_y15, or_3_out, or_6_out, or_7_out, or_8_out, or_9_out, or_10_out, or_11_out, or_12_out,
       or_13_out;

  decoder4_16 decoder4_16_1 (
    .A0(A0), .A1(A1), .A2(A2), .A3(A3), .Y0(decoder4_16_1_y0), .Y1(decoder4_16_1_y1), .Y2(decoder4_16_1_y2),
    .Y3(decoder4_16_1_y3), .Y4(decoder4_16_1_y4), .Y5(decoder4_16_1_y5), .Y6(decoder4_16_1_y6),
    .Y7(decoder4_16_1_y7), .Y8(decoder4_16_1_y8), .Y9(decoder4_16_1_y9), .Y10(decoder4_16_1_y10),
    .Y11(decoder4_16_1_y11), .Y12(decoder4_16_1_y12), .Y13(decoder4_16_1_y13), .Y14(decoder4_16_1_y14),
    .Y15(decoder4_16_1_y15));
  or or_1 (a, decoder4_16_1_y0, decoder4_16_1_y2, decoder4_16_1_y3, decoder4_16_1_y5, or_7_out, decoder4_16_1_y6, decoder4_16_1_y7, decoder4_16_1_y8, decoder4_16_1_y9);
  or or_2 (b, decoder4_16_1_y0, decoder4_16_1_y1, decoder4_16_1_y2, decoder4_16_1_y3, or_8_out, decoder4_16_1_y4, decoder4_16_1_y9, decoder4_16_1_y7, decoder4_16_1_y8);
  or or_3 (or_3_out, decoder4_16_1_y0, decoder4_16_1_y2, decoder4_16_1_y3, decoder4_16_1_y6, decoder4_16_1_y8, decoder4_16_1_y9, decoder4_16_1_y5);
  or or_4 (e, decoder4_16_1_y0, decoder4_16_1_y2, or_11_out, decoder4_16_1_y6, decoder4_16_1_y8);
  or or_5 (f, decoder4_16_1_y0, decoder4_16_1_y4, decoder4_16_1_y5, or_12_out, decoder4_16_1_y6, decoder4_16_1_y8, decoder4_16_1_y9);
  or or_6 (or_6_out, decoder4_16_1_y2, decoder4_16_1_y3, decoder4_16_1_y4, decoder4_16_1_y5, decoder4_16_1_y8, decoder4_16_1_y6, decoder4_16_1_y9);
  or or_7 (or_7_out, decoder4_16_1_y10, decoder4_16_1_y12, decoder4_16_1_y14, decoder4_16_1_y15);
  or or_8 (or_8_out, decoder4_16_1_y10, decoder4_16_1_y13);
  or or_9 (or_9_out, decoder4_16_1_y10, decoder4_16_1_y11, decoder4_16_1_y13);
  or or_10 (or_10_out, decoder4_16_1_y12, decoder4_16_1_y13, decoder4_16_1_y11, decoder4_16_1_y14);
  or or_11 (or_11_out, decoder4_16_1_y10, decoder4_16_1_y11, decoder4_16_1_y12, decoder4_16_1_y13, decoder4_16_1_y14, decoder4_16_1_y15);
  or or_12 (or_12_out, decoder4_16_1_y10, decoder4_16_1_y11, decoder4_16_1_y12, decoder4_16_1_y14, decoder4_16_1_y15);
  or or_13 (or_13_out, decoder4_16_1_y10, decoder4_16_1_y11, decoder4_16_1_y13, decoder4_16_1_y14, decoder4_16_1_y15);
  or or_14 (c, decoder4_16_1_y4, decoder4_16_1_y8, decoder4_16_1_y0, decoder4_16_1_y1, decoder4_16_1_y3, decoder4_16_1_y5, decoder4_16_1_y6, decoder4_16_1_y7, decoder4_16_1_y9, or_9_out);
  or or_15 (d, or_3_out, or_10_out);
  or or_16 (g, or_6_out, or_13_out);
endmodule

module fulladder_8_bit (
  input  A0,
  input  A1,
  input  A2,
  input  A3,
  input  A4,
  input  A5,
  input  A6,
  input  A7,
  input  B0,
  input  B1,
  input  B2,
  input  B3,
  input  B4,
  input  B5,
  input  B6,
  input  B7,
  output Light,
  output S0,
  output S1,
  output S2,
  output S3,
  output S4,
  output S5,
  output S6,
  output S7
);

  wire fulladder_1_bit_1_c1, fulladder_1_bit_2_c1, fulladder_1_bit_3_c1, fulladder_1_bit_4_c1,
       fulladder_1_bit_5_c1, fulladder_1_bit_6_c1, fulladder_1_bit_7_c1;

  fulladder_1_bit fulladder_1_bit_1 (.A(A0), .B(B0), .C1(fulladder_1_bit_1_c1), .S(S0));  // open: C
  fulladder_1_bit fulladder_1_bit_2 (.A(A1), .B(B1), .C(fulladder_1_bit_1_c1), .C1(fulladder_1_bit_2_c1), .S(S1));
  fulladder_1_bit fulladder_1_bit_3 (.A(A2), .B(B2), .C(fulladder_1_bit_2_c1), .C1(fulladder_1_bit_3_c1), .S(S2));
  fulladder_1_bit fulladder_1_bit_4 (.A(A3), .B(B3), .C(fulladder_1_bit_3_c1), .C1(fulladder_1_bit_4_c1), .S(S3));
  fulladder_1_bit fulladder_1_bit_5 (.A(A4), .B(B4), .C(fulladder_1_bit_4_c1), .C1(fulladder_1_bit_5_c1), .S(S4));
  fulladder_1_bit fulladder_1_bit_6 (.A(A5), .B(B5), .C(fulladder_1_bit_5_c1), .C1(fulladder_1_bit_6_c1), .S(S5));
  fulladder_1_bit fulladder_1_bit_7 (.A(A6), .B(B6), .C(fulladder_1_bit_6_c1), .C1(fulladder_1_bit_7_c1), .S(S6));
  fulladder_1_bit fulladder_1_bit_8 (.A(A7), .B(B7), .C(fulladder_1_bit_7_c1), .C1(Light), .S(S7));
  LED led_1 (.in(Light));
endmodule

module register_8_bit (
  input  reset,
  input  EN,
  input  D0,
  input  D1,
  input  D2,
  input  D3,
  input  D4,
  input  D5,
  input  D6,
  input  D7,
  output Q0,
  output Q1,
  output Q2,
  output Q3,
  output Q4,
  output Q5,
  output Q6,
  output Q7
);

  wire display_decoder_1_a, display_decoder_1_b, display_decoder_1_c, display_decoder_1_d,
       display_decoder_1_e, display_decoder_1_f, display_decoder_1_g, display_decoder_1_h,
       display_decoder_2_a, display_decoder_2_b, display_decoder_2_c, display_decoder_2_d,
       display_decoder_2_e, display_decoder_2_f, display_decoder_2_g, display_decoder_2_h, not_1_out;

  not not_1 (not_1_out, EN);
  Edge_TriggeredDFlip_Flop edge_triggereddflip_flop_1 (.D(D0), .CP(not_1_out), .reset(reset), .Q(Q0));
  Edge_TriggeredDFlip_Flop edge_triggereddflip_flop_2 (.D(D1), .CP(not_1_out), .reset(reset), .Q(Q1));
  Edge_TriggeredDFlip_Flop edge_triggereddflip_flop_3 (.D(D2), .CP(not_1_out), .reset(reset), .Q(Q2));
  Edge_TriggeredDFlip_Flop edge_triggereddflip_flop_4 (.D(D3), .CP(not_1_out), .reset(reset), .Q(Q3));
  Edge_TriggeredDFlip_Flop edge_triggereddflip_flop_5 (.D(D4), .CP(not_1_out), .reset(reset), .Q(Q4));
  Edge_TriggeredDFlip_Flop edge_triggereddflip_flop_6 (.D(D5), .CP(not_1_out), .reset(reset), .Q(Q5));
  Edge_TriggeredDFlip_Flop edge_triggereddflip_flop_7 (.D(D6), .CP(not_1_out), .reset(reset), .Q(Q6));
  Edge_TriggeredDFlip_Flop edge_triggereddflip_flop_8 (.D(D7), .CP(not_1_out), .reset(reset), .Q(Q7));
  display_decoder display_decoder_1 (
    .A0(Q0), .A1(Q1), .A2(Q2), .A3(Q3), .a(display_decoder_1_a), .b(display_decoder_1_b),
    .c(display_decoder_1_c), .d(display_decoder_1_d), .e(display_decoder_1_e), .f(display_decoder_1_f),
    .g(display_decoder_1_g), .h(display_decoder_1_h));
  display_decoder display_decoder_2 (
    .A0(Q4), .A1(Q5), .A2(Q6), .A3(Q7), .a(display_decoder_2_a), .b(display_decoder_2_b),
    .c(display_decoder_2_c), .d(display_decoder_2_d), .e(display_decoder_2_e), .f(display_decoder_2_f),
    .g(display_decoder_2_g), .h(display_decoder_2_h));
  _7_Segment_Display u_7_segment_display_1 (
    .g(display_decoder_2_g), .f(display_decoder_2_f), .a(display_decoder_2_a), .b(display_decoder_2_b),
    .e(display_decoder_2_e), .d(display_decoder_2_d), .c(display_decoder_2_c), .dp(display_decoder_2_h));
  _7_Segment_Display u_7_segment_display_2 (
    .g(display_decoder_1_g), .f(display_decoder_1_f), .a(display_decoder_1_a), .b(display_decoder_1_b),
    .e(display_decoder_1_e), .d(display_decoder_1_d), .c(display_decoder_1_c), .dp(display_decoder_1_h));
endmodule

module decoder_2_4 (
  input  in_1,
  input  in_2,
  output out_3,
  output out_4,
  output out_5,
  output out_6
);

  wire not_1_out, not_2_out, not_3_out, not_4_out;

  not not_1 (not_1_out, in_1);
  not not_2 (not_2_out, in_2);
  not not_3 (not_3_out, in_1);
  not not_4 (not_4_out, in_2);
  and and_1 (out_3, not_1_out, not_2_out);
  and and_2 (out_4, not_3_out, in_2);
  and and_3 (out_5, in_1, not_4_out);
  and and_4 (out_6, in_1, in_2);
endmodule

module Edge_TriggeredDFlip_Flop (
  input  D,
  input  CP,
  input  reset,
  output Q
);

  wire d_latch_1_q, not_1_out;

  not not_1 (not_1_out, CP);
  D_Latch d_latch_1 (.D(D), .EN(not_1_out), .reset(reset), .Q(d_latch_1_q));
  D_Latch d_latch_2 (.D(d_latch_1_q), .EN(CP), .reset(reset), .Q(Q));
endmodule

module D_Latch (
  input  D,
  input  EN,
  input  reset,
  output Q
);

  wire and_1_out, and_2_out, and_3_out, multiplexer1_2_1_1_out_4, nor_2_out, not_1_out, not_2_out;

  not not_1 (not_1_out, D);
  and and_1 (and_1_out, not_1_out, EN);
  and and_2 (and_2_out, EN, D);
  not not_2 (not_2_out, reset);
  and and_3 (and_3_out, and_2_out, not_2_out);
  multiplexer1_2_1 multiplexer1_2_1_1 (.D0(and_1_out), .S(reset), .D1(reset), .out_4(multiplexer1_2_1_1_out_4));
  nor nor_1 (Q, multiplexer1_2_1_1_out_4, nor_2_out);
  nor nor_2 (nor_2_out, Q, and_3_out);
endmodule

module multiplexer1_2_1 (
  input  D0,
  input  S,
  input  D1,
  output out_4
);

  wire and_1_out, and_2_out, not_1_out;

  not not_1 (not_1_out, S);
  and and_1 (and_1_out, D0, not_1_out);
  and and_2 (and_2_out, S, D1);
  or or_1 (out_4, and_1_out, and_2_out);
endmodule

module decoder4_16 (
  input  A0,
  input  A1,
  input  A2,
  input  A3,
  output Y0,
  output Y1,
  output Y2,
  output Y3,
  output Y4,
  output Y5,
  output Y6,
  output Y7,
  output Y8,
  output Y9,
  output Y10,
  output Y11,
  output Y12,
  output Y13,
  output Y14,
  output Y15
);

  wire decoder3_8_1_y0, decoder3_8_1_y1, decoder3_8_1_y2, decoder3_8_1_y3, decoder3_8_1_y4, decoder3_8_1_y5,
       decoder3_8_1_y6, decoder3_8_1_y7, not_1_out;

  not not_1 (not_1_out, A3);
  decoder3_8 decoder3_8_1 (
    .A0(A0), .A1(A1), .A2(A2), .Y0(decoder3_8_1_y0), .Y1(decoder3_8_1_y1), .Y2(decoder3_8_1_y2),
    .Y3(decoder3_8_1_y3), .Y4(decoder3_8_1_y4), .Y5(decoder3_8_1_y5), .Y6(decoder3_8_1_y6),
    .Y7(decoder3_8_1_y7));
  and and_1 (Y0, decoder3_8_1_y0, not_1_out);
  and and_2 (Y1, decoder3_8_1_y1, not_1_out);
  and and_3 (Y2, decoder3_8_1_y2, not_1_out);
  and and_4 (Y3, decoder3_8_1_y3, not_1_out);
  and and_5 (Y4, decoder3_8_1_y4, not_1_out);
  and and_6 (Y5, decoder3_8_1_y5, not_1_out);
  and and_7 (Y6, decoder3_8_1_y6, not_1_out);
  and and_8 (Y7, decoder3_8_1_y7, not_1_out);
  and and_9 (Y8, decoder3_8_1_y0, A3);
  and and_10 (Y9, decoder3_8_1_y1, A3);
  and and_11 (Y10, decoder3_8_1_y2, A3);
  and and_12 (Y11, decoder3_8_1_y3, A3);
  and and_13 (Y12, decoder3_8_1_y4, A3);
  and and_14 (Y13, decoder3_8_1_y5, A3);
  and and_15 (Y14, decoder3_8_1_y6, A3);
  and and_16 (Y15, decoder3_8_1_y7, A3);
endmodule

module decoder3_8 (
  input  A0,
  input  A1,
  input  A2,
  output Y0,
  output Y1,
  output Y2,
  output Y3,
  output Y4,
  output Y5,
  output Y6,
  output Y7
);

  wire decoder2_4_1_y0, decoder2_4_1_y1, decoder2_4_1_y2, decoder2_4_1_y3, not_1_out;

  not not_1 (not_1_out, A2);
  decoder2_4 decoder2_4_1 (
    .A0(A0), .A1(A1), .Y0(decoder2_4_1_y0), .Y1(decoder2_4_1_y1), .Y2(decoder2_4_1_y2), .Y3(decoder2_4_1_y3));
  and and_1 (Y0, decoder2_4_1_y0, not_1_out);
  and and_2 (Y1, not_1_out, decoder2_4_1_y1);
  and and_3 (Y2, decoder2_4_1_y2, not_1_out);
  and and_4 (Y3, decoder2_4_1_y3, not_1_out);
  and and_5 (Y4, A2, decoder2_4_1_y0);
  and and_6 (Y5, A2, decoder2_4_1_y1);
  and and_7 (Y6, A2, decoder2_4_1_y2);
  and and_8 (Y7, A2, decoder2_4_1_y3);
endmodule

module decoder2_4 (
  input  A0,
  input  A1,
  output Y0,
  output Y1,
  output Y2,
  output Y3
);

  wire not_1_out, not_2_out;

  not not_1 (not_1_out, A1);
  not not_2 (not_2_out, A0);
  and and_1 (Y0, not_1_out, not_2_out);
  and and_2 (Y1, not_1_out, A0);
  and and_3 (Y2, A1, not_2_out);
  and and_4 (Y3, A1, A0);
endmodule

module fulladder_1_bit (
  input  A,
  input  B,
  input  C,
  output C1,
  output S
);

  wire and_1_out, and_2_out, and_3_out, xor_1_out;

  and and_1 (and_1_out, A, B);
  and and_2 (and_2_out, A, C);
  and and_3 (and_3_out, B, C);
  xor xor_1 (xor_1_out, A, B);
  xor xor_2 (S, xor_1_out, C);
  or or_1 (C1, and_1_out, and_2_out, and_3_out);
endmodule
